// Logisim project Smart_traffic_Controller_Project.circ as structural Verilog: 1 circuit, main circuit main
module main (
  input  in_1,
  input  in_2,
  input  in_3
);

  wire and_1_out, clock_1_out, Emergency_EW_p1, Emergency_EW_p4, Emergency_NS_p1, Global_Clock_out,
       Night_Mode_p1, not_1_out, not_2_out, not_3_out, not_4_out, not_5_out, or_1_out, or_2_out, or_3_out,
       or_4_out, or_5_out, or_6_out, Register_1_q, States0_AND_out, States1_AND_out, States2_AND_out,
       States3_AND_out, Veh_NS_p1;
  wire [1:0] counter_1_q;
  wire [3:0] counter_2_q, EW_Timer_q, multiplexer_1_out, multiplexer_2_out, NS_Timer_q;

  Clock Global_Clock (.out(Global_Clock_out));
  Clock clock_1 (.out(clock_1_out));
  Button button_1 ();  // open: out
  // Switch Night_Mode: pin names not known; wires that end beside it: Night_Mode_p1, in_2
  Button Ped_EW ();  // open: out
  Button Reset (.out(Night_Mode_p1));
  // Switch Veh_NS: pin names not known; wires that end beside it: Veh_NS_p1
  // Switch Emergency_NS: pin names not known; wires that end beside it: Emergency_NS_p1
  // Switch Emergency_EW: pin names not known; wires that end beside it: Emergency_EW_p1, in_1, clock_1_out, Emergency_EW_p4
  Counter #(.max('hf), .width(4)) NS_Timer (
    .count(States0_AND_out), .clk(Global_Clock_out), .Q(NS_Timer_q));  // open: clr, load, up, D, carry
  Register #(.width(1)) Register_1 (.D(in_1), .clk(clock_1_out), .Q(Register_1_q), .clr(Emergency_EW_p4));  // open: en
  or or_1 (or_1_out, Emergency_NS_p1, Emergency_EW_p1);
  not not_1 (not_1_out, or_1_out);
  or or_2 (or_2_out, States2_AND_out, States3_AND_out);
  Counter #(.max('hf), .width(4)) EW_Timer (
    .count(States2_AND_out), .clk(Global_Clock_out), .Q(EW_Timer_q));  // open: clr, load, up, D, carry
  Comparator #(.width(4)) comparator_1 (.a(NS_Timer_q), .b(multiplexer_1_out));  // open: gt, eq, lt
  Counter #(.max('h3), .width(2)) counter_1 (
    .count(not_1_out), .clk(Global_Clock_out), .Q(counter_1_q));  // open: clr, load, up, D, carry
  and and_1 (and_1_out, Register_1_q, or_2_out);
  Counter #(.max('h9), .width(4)) counter_2 (
    .count(and_1_out), .clk(clock_1_out), .Q(counter_2_q));  // open: clr, load, up, D, carry
  Multiplexer #(.width(4)) multiplexer_1 (.in0(4'b0100), .in1(4'b1000), .out(multiplexer_1_out), .sel(Veh_NS_p1));
  Comparator #(.width(4)) comparator_2 (.a(EW_Timer_q), .b(multiplexer_2_out));  // open: gt, eq, lt
  not not_2 (not_2_out, counter_1_q[0]);
  not not_3 (not_3_out, counter_1_q[1]);
  not not_4 (not_4_out, counter_1_q[1]);
  not not_5 (not_5_out, counter_1_q[0]);
  Multiplexer #(.width(4)) multiplexer_2 (.in0(4'b0010), .in1(4'b1001), .out(multiplexer_2_out), .sel(in_3));
  and States0_AND (States0_AND_out, not_2_out, not_3_out);
  and States1_AND (States1_AND_out, counter_1_q[0], not_4_out);
  and States2_AND (States2_AND_out, counter_1_q[1], not_5_out);
  and States3_AND (States3_AND_out, counter_1_q[0], counter_1_q[1]);
  LED Night_NS ();  // open: in
  LED Night_EW ();  // open: in
  Hex_Digit_Display ped_Display_EW (.value(counter_2_q));  // open: dp
  or or_3 (or_3_out, States2_AND_out, States3_AND_out);
  or or_4 (or_4_out, States0_AND_out, Emergency_NS_p1);
  or or_5 (or_5_out, States0_AND_out, States1_AND_out);
  LED NS_Red (.in(or_3_out));
  LED NS_Yellow (.in(States1_AND_out));
  LED NS_Green (.in(or_4_out));
  or or_6 (or_6_out, or_5_out, Emergency_NS_p1);
  LED EW_Red (.in(or_6_out));
  LED EW_Yellow (.in(States3_AND_out));
  LED EW_Green (.in(States2_AND_out));

  // Notes on the sheet:
  //   in_1: pull=up, initial=0x9
endmodule
